// Logisim project Matriz leds conecta 4.circ as structural Verilog: 3 circuits, main circuit Color
module main (
  input  [1:0] Turno_de_Jugador
);

  wire [23:0] matriz_1_out_2, matriz_1_out_3, matriz_1_out_4, matriz_1_out_5, matriz_1_out_6, matriz_1_out_7,
       matriz_2_out_2, matriz_2_out_3, matriz_2_out_4, matriz_2_out_5, matriz_2_out_6, matriz_2_out_7,
       matriz_3_out_2, matriz_3_out_3, matriz_3_out_4, matriz_3_out_5, matriz_3_out_6, matriz_3_out_7,
       matriz_4_out_2, matriz_4_out_3, matriz_4_out_4, matriz_4_out_5, matriz_4_out_6, matriz_4_out_7,
       matriz_5_out_2, matriz_5_out_3, matriz_5_out_4, matriz_5_out_5, matriz_5_out_6, matriz_5_out_7,
       matriz_6_out_2, matriz_6_out_3, matriz_6_out_4, matriz_6_out_5, matriz_6_out_6, matriz_6_out_7,
       matriz_7_out_2, matriz_7_out_3, matriz_7_out_4, matriz_7_out_5, matriz_7_out_6, matriz_7_out_7;

  Button button_1 ();  // open: out
  Button button_2 ();  // open: out
  Matriz matriz_1 (
    .Circuito_de_validacion(Turno_de_Jugador), .out_2(matriz_1_out_2), .out_3(matriz_1_out_3),
    .out_4(matriz_1_out_4), .out_5(matriz_1_out_5), .out_6(matriz_1_out_6), .out_7(matriz_1_out_7));
  Matriz matriz_2 (
    .Circuito_de_validacion(Turno_de_Jugador), .out_2(matriz_2_out_2), .out_3(matriz_2_out_3),
    .out_4(matriz_2_out_4), .out_5(matriz_2_out_5), .out_6(matriz_2_out_6), .out_7(matriz_2_out_7));
  // RGBLed #(.multibit("true")) rgbled_1: pin names not known
  // RGBLed #(.multibit("true")) rgbled_2: pin names not known
  // RGBLed #(.multibit("true")) rgbled_3: pin names not known
  // RGBLed #(.multibit("true")) rgbled_4: pin names not known
  // RGBLed #(.multibit("true")) rgbled_5: pin names not known
  // RGBLed #(.multibit("true")) rgbled_6: pin names not known
  // RGBLed #(.multibit("true")) rgbled_7: pin names not known
  // RGBLed #(.multibit("true")) rgbled_8: pin names not known
  // RGBLed #(.multibit("true")) rgbled_9: pin names not known
  // RGBLed #(.multibit("true")) rgbled_10: pin names not known
  // RGBLed #(.multibit("true")) rgbled_11: pin names not known
  // RGBLed #(.multibit("true")) rgbled_12: pin names not known
  Button button_3 ();  // open: out
  Button button_4 ();  // open: out
  Matriz matriz_3 (
    .Circuito_de_validacion(Turno_de_Jugador), .out_2(matriz_3_out_2), .out_3(matriz_3_out_3),
    .out_4(matriz_3_out_4), .out_5(matriz_3_out_5), .out_6(matriz_3_out_6), .out_7(matriz_3_out_7));
  Matriz matriz_4 (
    .Circuito_de_validacion(Turno_de_Jugador), .out_2(matriz_4_out_2), .out_3(matriz_4_out_3),
    .out_4(matriz_4_out_4), .out_5(matriz_4_out_5), .out_6(matriz_4_out_6), .out_7(matriz_4_out_7));
  // RGBLed #(.multibit("true")) rgbled_13: pin names not known
  // RGBLed #(.multibit("true")) rgbled_14: pin names not known
  // RGBLed #(.multibit("true")) rgbled_15: pin names not known
  // RGBLed #(.multibit("true")) rgbled_16: pin names not known
  // RGBLed #(.multibit("true")) rgbled_17: pin names not known
  // RGBLed #(.multibit("true")) rgbled_18: pin names not known
  Button button_5 ();  // open: out
  Matriz matriz_5 (
    .Circuito_de_validacion(Turno_de_Jugador), .out_2(matriz_5_out_2), .out_3(matriz_5_out_3),
    .out_4(matriz_5_out_4), .out_5(matriz_5_out_5), .out_6(matriz_5_out_6), .out_7(matriz_5_out_7));
  // RGBLed #(.multibit("true")) rgbled_19: pin names not known
  // RGBLed #(.multibit("true")) rgbled_20: pin names not known
  // RGBLed #(.multibit("true")) rgbled_21: pin names not known
  // RGBLed #(.multibit("true")) rgbled_22: pin names not known
  // RGBLed #(.multibit("true")) rgbled_23: pin names not known
  // RGBLed #(.multibit("true")) rgbled_24: pin names not known
  // RGBLed #(.multibit("true")) rgbled_25: pin names not known
  // RGBLed #(.multibit("true")) rgbled_26: pin names not known
  // RGBLed #(.multibit("true")) rgbled_27: pin names not known
  // RGBLed #(.multibit("true")) rgbled_28: pin names not known
  // RGBLed #(.multibit("true")) rgbled_29: pin names not known
  // RGBLed #(.multibit("true")) rgbled_30: pin names not known
  Button button_6 ();  // open: out
  Button button_7 ();  // open: out
  Matriz matriz_6 (
    .Circuito_de_validacion(Turno_de_Jugador), .out_2(matriz_6_out_2), .out_3(matriz_6_out_3),
    .out_4(matriz_6_out_4), .out_5(matriz_6_out_5), .out_6(matriz_6_out_6), .out_7(matriz_6_out_7));
  Matriz matriz_7 (
    .Circuito_de_validacion(Turno_de_Jugador), .out_2(matriz_7_out_2), .out_3(matriz_7_out_3),
    .out_4(matriz_7_out_4), .out_5(matriz_7_out_5), .out_6(matriz_7_out_6), .out_7(matriz_7_out_7));
  // RGBLed #(.multibit("true")) rgbled_31: pin names not known
  // RGBLed #(.multibit("true")) rgbled_32: pin names not known
  // RGBLed #(.multibit("true")) rgbled_33: pin names not known
  // RGBLed #(.multibit("true")) rgbled_34: pin names not known
  // RGBLed #(.multibit("true")) rgbled_35: pin names not known
  // RGBLed #(.multibit("true")) rgbled_36: pin names not known
  // RGBLed #(.multibit("true")) rgbled_37: pin names not known
  // RGBLed #(.multibit("true")) rgbled_38: pin names not known
  // RGBLed #(.multibit("true")) rgbled_39: pin names not known
  // RGBLed #(.multibit("true")) rgbled_40: pin names not known
  // RGBLed #(.multibit("true")) rgbled_41: pin names not known
  // RGBLed #(.multibit("true")) rgbled_42: pin names not known
endmodule

module Matriz (
  input  [1:0] Circuito_de_validacion,
  output [23:0] out_2,
  output [23:0] out_3,
  output [23:0] out_4,
  output [23:0] out_5,
  output [23:0] out_6,
  output [23:0] out_7
);

  wire [1:0] register_1_q, register_2_q, register_3_q, register_4_q, register_5_q, register_6_q;

  Register #(.width(2), .Select("low")) register_1 (.Q(register_1_q));  // open: D, en, clk, clr
  Color color_1 (.Jugador(register_1_q), .RGB(out_2));
  Register #(.width(2), .Select("low")) register_2 (.Q(register_2_q));  // open: D, en, clk, clr
  Color color_2 (.Jugador(register_2_q), .RGB(out_3));
  Register #(.width(2), .Select("low")) register_3 (.Q(register_3_q));  // open: D, en, clk, clr
  Color color_3 (.Jugador(register_3_q), .RGB(out_4));
  Register #(.width(2), .Select("low")) register_4 (.Q(register_4_q));  // open: D, en, clk, clr
  Color color_4 (.Jugador(register_4_q), .RGB(out_5));
  Register #(.width(2), .Select("low")) register_5 (.Q(register_5_q));  // open: D, en, clk, clr
  Color color_5 (.Jugador(register_5_q), .RGB(out_6));
  Register #(.width(2), .Select("low")) register_6 (.Q(register_6_q));  // open: D, en, clk, clr
  Color color_6 (.Jugador(register_6_q), .RGB(out_7));
endmodule

module Color (
  input  [1:0] Jugador,
  output [23:0] RGB
);

  // RGBLed #(.multibit("true")) rgbled_1: pin names not known
  Multiplexer #(.select(2), .width(24), .enable("false")) multiplexer_1 (
    .in0({24{1'b0}}), .in1(24'hf9fc06), .in2(24'hff0000), .out(RGB), .sel(Jugador));  // open: in3
endmodule
